// Logisim project main.circ as structural Verilog: 3 circuits, main circuit main
module main (
);

  N_bit_MUX n_bit_mux_1 ();  // open: a, b, s, o
endmodule

module N_bit_MUX (
  input  [3:0] a,
  input  [3:0] b,
  input  s,
  output [3:0] o
);

  Multiplexer multiplexer_1 (.in0(b[3]), .in1(a[3]), .out(o[3]), .sel(s));
  Multiplexer multiplexer_2 (.in0(b[2]), .in1(a[2]), .out(o[2]), .sel(s));
  Multiplexer multiplexer_3 (.in0(b[1]), .in1(a[1]), .out(o[1]), .sel(s));
  Multiplexer multiplexer_4 (.in0(b[0]), .in1(a[0]), .out(o[0]), .sel(s));
endmodule

module N_bit_shift_register (
  input  [3:0] D,
  input  load,
  input  A,
  input  shift
);

  wire clock_1_out, clock_2_out, clock_3_out, clock_4_out;
  wire [3:0] d_ff_1_q, n_bit_mux_1_o, n_bit_mux_2_o;

  // Shift_Register #(.length(4)) shift_register_1: pin names not known
  D_Flip_Flop d_ff_1 (.D(n_bit_mux_2_o[3]), .clk(clock_1_out), .Q(d_ff_1_q[3]));  // open: Qn, preset, reset
  Clock clock_1 (.out(clock_1_out));
  N_bit_MUX n_bit_mux_1 (.a(D), .b(d_ff_1_q), .s(load), .o(n_bit_mux_1_o));
  D_Flip_Flop d_ff_2 (.D(n_bit_mux_2_o[2]), .clk(clock_2_out), .Q(d_ff_1_q[2]));  // open: Qn, preset, reset
  Clock clock_2 (.out(clock_2_out));
  N_bit_MUX n_bit_mux_2 (.a({d_ff_1_q[2:0], A}), .b(n_bit_mux_1_o), .s(shift), .o(n_bit_mux_2_o));
  D_Flip_Flop d_ff_3 (.D(n_bit_mux_2_o[1]), .clk(clock_3_out), .Q(d_ff_1_q[1]));  // open: Qn, preset, reset
  Clock clock_3 (.out(clock_3_out));
  Clock clock_4 (.out(clock_4_out));
  D_Flip_Flop d_ff_4 (.D(n_bit_mux_2_o[0]), .clk(clock_4_out), .Q(d_ff_1_q[0]));  // open: Qn, preset, reset
endmodule
